# Fritzing sketch pendulum_electronics (saved by Fritzing 0.9.2b)
breadboards: 1

parts:
  Part1 = Arduino Mega ADK (Rev3)
  C1 = Electrolytic Capacitor [capacitance=1µF package="100 mil [THT, electrolytic]"]
  Modified_Servo = DC Motor
  IC2 = L293D [package=THT]
  including_potentiometer_and_motor = Rotary Potentiometer (Small) [maximum_resistance=100kΩ package=THT]
  Part2 = ACS712 Low Current Sensor Board v12
  Part3 = IMU Digital Combo Board 6DOF
  Power_plug1 = Power plug

nets:
  N1: Part1.A0, including_potentiometer_and_motor.wiper
  N2: Part1.A1, Part2.VO
  N3: Part1.D21/SCL, Part3.SDA
  N4: Part1.D20/SDA, Part3.SCL
  N5: Part1.D10_PWM, IC2.Enable_1
  N6: Part1.D8_PWM, IC2.In_1
  3V3: Part1.3V3, Part3.3.3V
  5V: Part1.5V, C1.+, IC2.+V, including_potentiometer_and_motor.leg2, Part2.5V
  GND: Part1.GND, C1.-, IC2.0V, including_potentiometer_and_motor.leg1, Part2.GND, Part3.GND, Power_plug1.GND
  N7: Part1.D2_PWM, Part3.INT0
  N8: Part1.D7_PWM, IC2.In_2
  N9: Modified_Servo.pin_1, IC2.Out_1_(_Controlled_by_Enable_1_)
  N10: Modified_Servo.pin_2, Part2.IP-
  N11: IC2.Out_2_(_Controlled_by_Enable_1_), Part2.IP+
  N12: IC2.+Vmotor, Power_plug1.VCC
